// Logisim project Single Cycle Processor.circ as structural Verilog: 4 circuits, main circuit main
module main (
  input  in_1
);

  wire ALUSrc, Clk, ExtOp, MemRd, MemWr, RegDst, RegWr, WBdata, ZeroFlag;
  wire [1:0] PCSrc;
  wire [2:0] Funct, multiplexer_3_out;
  wire [3:0] ALUOp, Opcode;
  wire [8:0] ram_1_data;
  wire [11:0] adder_1_out, adder_2_out, bit_extender_1_out, bit_extender_2_out, multiplexer_1_out,
       multiplexer_2_out, register_1_q, undriven;
  wire [15:0] ALU_aluresult, bit_extender_3_out, bit_extender_4_out, file_register_1_busa,
       file_register_1_busb, multiplexer_4_out, multiplexer_5_out, multiplexer_6_out, ram_2_data;

  Multiplexer #(.select(2), .width(12), .enable("false")) multiplexer_1 (
    .in0(adder_1_out), .in1({Funct, ram_1_data}), .in2(adder_2_out), .in3(undriven), .out(multiplexer_1_out),
    .sel(PCSrc));
  Register #(.width(12)) register_1 (.D(multiplexer_1_out), .Q(register_1_q), .clk(Clk), .clr(in_1));  // open: en
  Adder #(.width(12)) adder_1 (.a(12'h1), .b(register_1_q), .out(adder_1_out));  // open: cin, cout
  // PC_Control PC_Control: pin names not known; wires that end beside it: ZeroFlag
  Clock clock_1 (.out(Clk));
  RAM #(.addrWidth(12), .dataWidth(16)) ram_1 (
    .addr(register_1_q), .data({Funct, ram_1_data, Opcode}), .clk(Clk));  // open: sel, ld, clr
  assign bit_extender_1_out = {{6{Funct[2]}}, {Funct, ram_1_data[8:6]}};  // Bit_Extender bit_extender_1
  assign bit_extender_2_out = {{6{1'b0}}, {Funct, ram_1_data[8:6]}};  // Bit_Extender bit_extender_2
  Multiplexer #(.width(12), .enable("false")) multiplexer_2 (
    .in0(bit_extender_1_out), .in1(bit_extender_2_out), .out(multiplexer_2_out), .sel(ExtOp));
  Multiplexer #(.width(3), .enable("false")) multiplexer_3 (
    .in0(ram_1_data[5:3]), .in1(ram_1_data[8:6]), .out(multiplexer_3_out), .sel(RegDst));
  // Main_Control main_control_1: pin names not known; wires that end beside it: Opcode[3], Opcode[2], Opcode[1], Opcode[0], RegDst, RegWr, ExtOp, ALUSrc, MemRd, MemWr, WBdata
  assign bit_extender_3_out = {{4{1'b0}}, multiplexer_2_out};  // Bit_Extender bit_extender_3
  Multiplexer #(.width(16), .enable("false")) multiplexer_4 (
    .in0(bit_extender_3_out), .in1(bit_extender_4_out), .out(multiplexer_4_out), .sel(ExtOp));
  assign bit_extender_4_out = {{4{multiplexer_2_out[11]}}, multiplexer_2_out};  // Bit_Extender bit_extender_4
  File_Register file_register_1 (
    .BusW(multiplexer_6_out), .RegWrite(RegWr), .RA(ram_1_data[2:0]), .RB(ram_1_data[5:3]),
    .BusA(file_register_1_busa), .BusB(file_register_1_busb), .RW(multiplexer_3_out), .Clock(Clk));
  Adder #(.width(12)) adder_2 (.a(adder_1_out), .b(multiplexer_2_out), .out(adder_2_out));  // open: cin, cout
  Multiplexer #(.width(16), .enable("false")) multiplexer_5 (
    .in0(file_register_1_busb), .in1(multiplexer_4_out), .out(multiplexer_5_out), .sel(ALUSrc));
  ALU ALU (
    .A(file_register_1_busa), .ALUOp(ALUOp), .ZeroFlag(ZeroFlag), .B(multiplexer_5_out),
    .ALUResult(ALU_aluresult));
  RAM #(.addrWidth(16), .dataWidth(16), .bus("separate")) ram_2 (
    .addr(ALU_aluresult), .din(file_register_1_busb), .data(ram_2_data), .str(MemRd), .clk(Clk), .ld(MemWr));  // open: sel, clr
  // ALU_Control alu_control_1: pin names not known; wires that end beside it: Opcode[3], Opcode[2], Opcode[1], Opcode[0]
  Multiplexer #(.width(16), .enable("false")) multiplexer_6 (
    .in0(ALU_aluresult), .in1(ram_2_data), .out(multiplexer_6_out), .sel(WBdata));
endmodule

module ALU (
  input  [3:0] ALUOp,
  input  [15:0] A,
  input  [15:0] B,
  output [15:0] ALUResult,
  output ZeroFlag
);

  wire [15:0] adder_1_out, and_1_out, nor_1_out, not_1_out, or_1_out, shifter_1_out, shifter_2_out,
       shifter_3_out, shifter_4_out, subtractor_1_out, undriven, undriven_2, undriven_3, undriven_4,
       undriven_5, undriven_6;

  assign or_1_out = A | B;  // OR_Gate or_1, 16 bits wide
  assign and_1_out = A & B;  // AND_Gate and_1, 16 bits wide
  assign not_1_out = ~and_1_out;  // NOT_Gate not_1, 16 bits wide
  assign nor_1_out = ~(A | B);  // NOR_Gate nor_1, 16 bits wide
  Adder #(.width(16)) adder_1 (.a(A), .b(B), .out(adder_1_out));  // open: cin, cout
  Subtractor #(.width(16)) subtractor_1 (.a(A), .b(B), .out(subtractor_1_out));  // open: bin, bout
  Shifter_part #(.width(16)) shifter_1 (.in(A), .\dist (B[3:0]), .out(shifter_1_out));
  Shifter_part #(.width(16), .shift("lr")) shifter_2 (.in(A), .\dist (B[3:0]), .out(shifter_2_out));
  Shifter_part #(.width(16), .shift("ar")) shifter_3 (.in(A), .\dist (B[3:0]), .out(shifter_3_out));
  Shifter_part #(.width(16), .shift("rr")) shifter_4 (.in(A), .\dist (B[3:0]), .out(shifter_4_out));
  Multiplexer #(.select(4), .width(16), .enable("false")) multiplexer_1 (
    .in0(or_1_out), .in1(and_1_out), .in2(not_1_out), .in3(nor_1_out), .in4(adder_1_out),
    .in5(subtractor_1_out), .in6(shifter_1_out), .in7(shifter_2_out), .in8(shifter_3_out),
    .in9(shifter_4_out), .in10(undriven), .in11(undriven_2), .in12(undriven_3), .in13(undriven_4),
    .in14(undriven_5), .in15(undriven_6), .out(ALUResult), .sel(ALUOp));
  Comparator #(.width(16)) comparator_1 (.a(subtractor_1_out), .b({16{1'b0}}), .eq(ZeroFlag));  // open: gt, lt
endmodule

module Shifter (
  input  [15:0] Data,
  input  [3:0] Shift_amount,
  input  [1:0] Shift_Op,
  output [15:0] Data_out
);

  wire [15:0] shifter_1_out, shifter_2_out, shifter_3_out, shifter_4_out;

  Shifter_part #(.width(16)) shifter_1 (.in(Data), .\dist (Shift_amount), .out(shifter_1_out));
  Shifter_part #(.width(16), .shift("lr")) shifter_2 (.in(Data), .\dist (Shift_amount), .out(shifter_2_out));
  Shifter_part #(.width(16), .shift("ar")) shifter_3 (.in(Data), .\dist (Shift_amount), .out(shifter_3_out));
  Shifter_part #(.width(16), .shift("rr")) shifter_4 (.in(Data), .\dist (Shift_amount), .out(shifter_4_out));
  Multiplexer #(.select(2), .width(16), .enable("false")) multiplexer_1 (
    .in0(shifter_1_out), .in1(shifter_2_out), .in2(shifter_3_out), .in3(shifter_4_out), .out(Data_out),
    .sel(Shift_Op));
endmodule

module File_Register (
  input  [2:0] RA,
  input  [2:0] RB,
  input  [2:0] RW,
  input  [15:0] BusW,
  input  RegWrite,
  input  Clock,
  output [15:0] BusA,
  output [15:0] BusB
);

  wire and_1_out, and_2_out, and_3_out, and_4_out, and_5_out, and_6_out, and_7_out, decoder_1_out0,
       decoder_1_out1, decoder_1_out2, decoder_1_out3, decoder_1_out4, decoder_1_out5, decoder_1_out6,
       decoder_1_out7, decoder_2_out0, decoder_2_out1, decoder_2_out2, decoder_2_out3, decoder_2_out4,
       decoder_2_out5, decoder_2_out6, decoder_2_out7, decoder_3_out0, decoder_3_out1, decoder_3_out2,
       decoder_3_out3, decoder_3_out4, decoder_3_out5, decoder_3_out6, decoder_3_out7;
  wire [15:0] R1_q, R2_q, R3_q, R4_q, R5_q, R6_q;

  Decoder #(.select(3), .enable("false")) decoder_1 (
    .out0(decoder_1_out0), .out1(decoder_1_out1), .out2(decoder_1_out2), .out3(decoder_1_out3),
    .out4(decoder_1_out4), .out5(decoder_1_out5), .out6(decoder_1_out6), .out7(decoder_1_out7), .sel(RW));
  Register #(.width(16)) R1 (.D(BusW), .en(and_1_out), .Q(R1_q), .clk(Clock));  // open: clr
  and and_1 (and_1_out, decoder_1_out1, RegWrite);
  Register #(.width(16)) R2 (.D(BusW), .en(and_2_out), .Q(R2_q), .clk(Clock));  // open: clr
  and and_2 (and_2_out, decoder_1_out2, RegWrite);
  Register #(.width(16)) R3 (.D(BusW), .en(and_3_out), .Q(R3_q), .clk(Clock));  // open: clr
  and and_3 (and_3_out, decoder_1_out3, RegWrite);
  Register #(.width(16)) R4 (.D(BusW), .en(and_4_out), .Q(R4_q), .clk(Clock));  // open: clr
  and and_4 (and_4_out, decoder_1_out4, RegWrite);
  Register #(.width(16)) R5 (.D(BusW), .en(and_5_out), .Q(R5_q), .clk(Clock));  // open: clr
  and and_5 (and_5_out, decoder_1_out5, RegWrite);
  Register #(.width(16)) R6 (.D(BusW), .en(and_6_out), .Q(R6_q), .clk(Clock));  // open: clr
  and and_6 (and_6_out, decoder_1_out6, RegWrite);
  Register #(.width(16)) R7 (.D(BusW), .en(and_7_out), .Q(BusA), .clk(Clock));  // open: clr
  and and_7 (and_7_out, decoder_1_out7, RegWrite);
  Decoder #(.select(3), .enable("false")) decoder_2 (
    .out0(decoder_2_out0), .out1(decoder_2_out1), .out2(decoder_2_out2), .out3(decoder_2_out3),
    .out4(decoder_2_out4), .out5(decoder_2_out5), .out6(decoder_2_out6), .out7(decoder_2_out7), .sel(RA));
  assign BusA = decoder_2_out1 ? R1_q : 16'bz;  // Controlled_Buffer controlled_buffer_1
  assign BusA = decoder_2_out2 ? R2_q : 16'bz;  // Controlled_Buffer controlled_buffer_2
  assign BusA = decoder_2_out3 ? R3_q : 16'bz;  // Controlled_Buffer controlled_buffer_3
  assign BusA = decoder_2_out4 ? R4_q : 16'bz;  // Controlled_Buffer controlled_buffer_4
  assign BusA = decoder_2_out5 ? R5_q : 16'bz;  // Controlled_Buffer controlled_buffer_5
  assign BusA = decoder_2_out6 ? R6_q : 16'bz;  // Controlled_Buffer controlled_buffer_6
  assign BusA = decoder_2_out7 ? BusA : 16'bz;  // Controlled_Buffer controlled_buffer_7
  assign BusA = decoder_2_out0 ? {16{1'b0}} : 16'bz;  // Controlled_Buffer controlled_buffer_8
  Decoder #(.select(3), .enable("false")) decoder_3 (
    .out0(decoder_3_out0), .out1(decoder_3_out1), .out2(decoder_3_out2), .out3(decoder_3_out3),
    .out4(decoder_3_out4), .out5(decoder_3_out5), .out6(decoder_3_out6), .out7(decoder_3_out7), .sel(RB));
  assign BusB = decoder_3_out0 ? {16{1'b0}} : 16'bz;  // Controlled_Buffer controlled_buffer_9
  assign BusB = decoder_3_out1 ? R1_q : 16'bz;  // Controlled_Buffer controlled_buffer_10
  assign BusB = decoder_3_out2 ? R2_q : 16'bz;  // Controlled_Buffer controlled_buffer_11
  assign BusB = decoder_3_out3 ? R3_q : 16'bz;  // Controlled_Buffer controlled_buffer_12
  assign BusB = decoder_3_out4 ? R4_q : 16'bz;  // Controlled_Buffer controlled_buffer_13
  assign BusB = decoder_3_out5 ? R5_q : 16'bz;  // Controlled_Buffer controlled_buffer_14
  assign BusB = decoder_3_out6 ? R6_q : 16'bz;  // Controlled_Buffer controlled_buffer_15
  assign BusB = decoder_3_out7 ? BusA : 16'bz;  // Controlled_Buffer controlled_buffer_16
endmodule
